// Logisim project g1-2.circ as structural Verilog: 6 circuits, main circuit main
module main (
  input  [3:0] ALUOperation,
  input  [3:0] A,
  input  [3:0] B,
  input  [3:0] ALUOperation_2,
  output Zero,
  output [3:0] Result,
  output Overflow
);

  wire alu_4_bit_2_overflow, alu_4_bit_2_zero, and_1_out, and_2_out, and_3_out, clock_1_out, comparator_1_eq,
       comparator_2_eq, mips_alu_4_bit_1_p4, mips_alu_4_bit_1_p6, multiplexer_1_out, not_1_out, not_2_out,
       xnor_1_out;
  wire [3:0] alu_4_bit_2_result, mips_alu_4_bit_1_p5, random_1_out, random_2_out;

  Clock clock_1 (.out(clock_1_out));
  Random #(.width(4)) random_1 (.clk(clock_1_out), .next(multiplexer_1_out), .out(random_1_out));  // open: clr
  Random #(.width(4), .seed(1)) random_2 (
    .clk(clock_1_out), .next(multiplexer_1_out), .out(random_2_out));  // open: clr
  ALU__4_bit alu_4_bit_1 (
    .A(A), .B(B), .Result(Result), .Overflow(Overflow), .Zero(Zero), .ALUOperationl(ALUOperation));
  ALU__4_bit alu_4_bit_2 (
    .A(random_1_out), .B(random_2_out), .Result(alu_4_bit_2_result), .Overflow(alu_4_bit_2_overflow),
    .Zero(alu_4_bit_2_zero), .ALUOperationl(ALUOperation_2));
  // MIPS_ALU_4_bit mips_alu_4_bit_1: pin names not known; wires that end beside it: random_1_out, random_2_out, ALUOperation_2, mips_alu_4_bit_1_p4, mips_alu_4_bit_1_p5, mips_alu_4_bit_1_p6
  not not_1 (not_1_out, ALUOperation_2[0]);
  and and_1 (and_1_out, not_1_out, ALUOperation_2[1]);
  xnor xnor_1 (xnor_1_out, alu_4_bit_2_zero, mips_alu_4_bit_1_p4);
  and and_2 (and_2_out, xnor_1_out, comparator_1_eq);
  Comparator #(.width(4)) comparator_1 (
    .a(alu_4_bit_2_result), .b(mips_alu_4_bit_1_p5), .eq(comparator_1_eq));  // open: gt, lt
  and and_3 (and_3_out, comparator_1_eq, comparator_2_eq);
  Comparator #(.width(1)) comparator_2 (
    .a(alu_4_bit_2_overflow), .b(mips_alu_4_bit_1_p6), .eq(comparator_2_eq));  // open: gt, lt
  Multiplexer #(.enable("false")) multiplexer_1 (
    .in0(and_2_out), .in1(and_3_out), .out(multiplexer_1_out), .sel(and_1_out));
  not not_2 (not_2_out, multiplexer_1_out);
  LED led_1 (.in(not_2_out));

  // Notes on the sheet:
  //   Manual test
  //   Automatic test
  //   Black box ALU
  //   Stop generating new examples on error
  //   Only compare overflow bit on add or subtract
  //   Black = ok
  //   Red = error
endmodule

module ALU__4_bit (
  input  [3:0] ALUOperationl,
  input  [3:0] A,
  input  [3:0] B,
  output Zero,
  output [3:0] Result,
  output Overflow
);
endmodule

module Multiplexor__2_in__1_bit (
  input  in_1,
  input  in_2,
  input  in_3,
  output out_4
);

  wire and_1_out, and_2_out;

  and and_1 (and_1_out, in_2, ~in_1);  // AND_Gate
  or or_1 (out_4, and_1_out, and_2_out);
  and and_2 (and_2_out, in_1, in_3);
endmodule

module Multiplexor__4_in__1_bit (
  input  [1:0] in_1,
  input  in_2,
  input  in_3,
  input  in_4,
  input  in_5,
  output out_6
);

  wire multiplexor_2_in_1_bit_1_out_4, multiplexor_2_in_1_bit_2_out_4;

  Multiplexor__2_in__1_bit multiplexor_2_in_1_bit_1 (
    .in_2(in_2), .in_3(in_3), .out_4(multiplexor_2_in_1_bit_1_out_4), .in_1(in_1[0]));
  Multiplexor__2_in__1_bit multiplexor_2_in_1_bit_2 (
    .in_2(in_4), .in_3(in_5), .out_4(multiplexor_2_in_1_bit_2_out_4), .in_1(in_1[0]));
  Multiplexor__2_in__1_bit multiplexor_2_in_1_bit_3 (
    .in_2(multiplexor_2_in_1_bit_1_out_4), .in_3(multiplexor_2_in_1_bit_2_out_4), .out_4(out_6),
    .in_1(in_1[1]));
endmodule

module Adder__1_bit (
  input  in_1,
  input  in_2,
  input  in_3,
  output out_4
);

  wire and_1_out, and_2_out, and_3_out;

  and and_1 (and_1_out, in_1, in_2);
  and and_2 (and_2_out, in_1, in_3);
  and and_3 (and_3_out, in_2, in_3);
  or or_1 (out_4, and_1_out, and_2_out, and_3_out);
endmodule

module ALU__1_bit (
  input  in_1,
  input  in_2,
  input  in_3,
  input  [1:0] in_4,
  input  in_5,
  input  in_6,
  input  in_7,
  output out_8
);

  wire adder_1_bit_1_out_4, and_1_out, multiplexor_2_in_1_bit_1_out_4, multiplexor_2_in_1_bit_2_out_4,
       not_1_out, not_2_out, or_1_out;

  Multiplexor__2_in__1_bit multiplexor_2_in_1_bit_1 (
    .in_2(in_5), .in_3(not_1_out), .out_4(multiplexor_2_in_1_bit_1_out_4), .in_1(in_1));
  not not_1 (not_1_out, in_5);
  Multiplexor__2_in__1_bit multiplexor_2_in_1_bit_2 (
    .in_2(in_6), .in_3(not_2_out), .out_4(multiplexor_2_in_1_bit_2_out_4), .in_1(in_2));
  not not_2 (not_2_out, in_6);
  and and_1 (and_1_out, multiplexor_2_in_1_bit_1_out_4, multiplexor_2_in_1_bit_2_out_4);
  or or_1 (or_1_out, multiplexor_2_in_1_bit_1_out_4, multiplexor_2_in_1_bit_2_out_4);
  Adder__1_bit adder_1_bit_1 (
    .in_2(multiplexor_2_in_1_bit_1_out_4), .in_3(multiplexor_2_in_1_bit_2_out_4), .in_1(in_3),
    .out_4(adder_1_bit_1_out_4));
  Multiplexor__4_in__1_bit multiplexor_4_in_1_bit_1 (
    .in_1(in_4), .in_2(and_1_out), .in_3(or_1_out), .in_5(in_7), .out_6(out_8));  // open: in_4

  // Notes on the sheet:
  //   carryout xPx xPX XPXPX
endmodule
