// Logisim project g2-1.circ as structural Verilog: 1 circuit, main circuit main
module main (
  input  in_1
);

  wire clock;
  wire [31:0] mipsprogramrom_1_p2, PC_q;

  Register #(.width(32)) PC (.Q(PC_q), .clk(clock), .clr(in_1));  // open: D, en
  Clock clock_1 (.out(clock));
  // MIPSProgramROM mipsprogramrom_1: pin names not known; wires that end beside it: PC_q, mipsprogramrom_1_p2, clock
  // RegisterFile registerfile_1: pin names not known; wires that end beside it: in_1
  // MIPS_ALU mips_alu_1: pin names not known
  // MIPS_RAM mips_ram_1: pin names not known; wires that end beside it: clock, in_1

  // Other names for the same wires on the sheet: reset = in_1

  // Notes on the sheet:
  //   address
  //   rs
  //   rt
  //   rd
  //   immediate
  //   shamt
  //   funct
  //   opcode
endmodule
