// Logisim project g2-1_soeren.circ as structural Verilog: 1 circuit, main circuit main
module main (
  input  in_1
);

  wire ALU_Control_p2, and_1_out, clock, mips_alu_1_p4, registerfile_1_p5;
  wire [4:0] multiplexer_1_out;
  wire [10:0] Control_p2;
  wire [31:0] adder_1_p3, adder_1_p4, adder_2_p3, bit_extender_1_out, bit_extender_2_out, mips_alu_1_p5,
       mips_ram_1_p4, mipsprogramrom_1_p3, multiplexer_2_out, multiplexer_3_out, multiplexer_4_out, PC_q,
       registerfile_1_p6;

  Register #(.width(32)) PC (.D(multiplexer_4_out), .Q(PC_q), .clk(clock), .clr(in_1));  // open: en
  // Adder adder_1: pin names not known; wires that end beside it: PC_q, 32'h4, adder_1_p3, adder_1_p4[25:0]
  Clock clock_1 (.out(clock));
  // MIPSProgramROM mipsprogramrom_1: pin names not known; wires that end beside it: PC_q, adder_1_p4, mipsprogramrom_1_p3, clock, Control_p2[9]
  // PLA Control: pin names not known; wires that end beside it: adder_1_p4[31:26], Control_p2, adder_1_p4[10:6]
  Multiplexer #(.width(5), .enable("false")) multiplexer_1 (
    .in0(adder_1_p4[20:16]), .in1(adder_1_p4[15:11]), .out(multiplexer_1_out), .sel(Control_p2[0]));
  // RegisterFile registerfile_1: pin names not known; wires that end beside it: multiplexer_1_out, adder_1_p4[25:21], adder_1_p4[20:16], in_1, registerfile_1_p5, registerfile_1_p6
  assign bit_extender_1_out = {{16{adder_1_p4[15]}}, adder_1_p4[15:0]};  // Bit_Extender bit_extender_1
  Multiplexer #(.width(32), .enable("false")) multiplexer_2 (
    .in0(bit_extender_1_out), .in1(bit_extender_2_out), .out(multiplexer_2_out), .sel(Control_p2[10]));
  assign bit_extender_2_out = {{16{1'b0}}, adder_1_p4[15:0]};  // Bit_Extender bit_extender_2
  Multiplexer #(.width(32), .enable("false")) multiplexer_3 (
    .in0(registerfile_1_p6), .in1(multiplexer_2_out), .out(multiplexer_3_out), .sel(Control_p2[8]));
  // PLA ALU_Control: pin names not known; wires that end beside it: {Control_p2[6:4], adder_1_p4[5:0]}, ALU_Control_p2
  // Adder adder_2: pin names not known; wires that end beside it: adder_1_p3, {multiplexer_2_out[29:0], 2'b00}, adder_2_p3
  and and_1 (and_1_out, mips_alu_1_p4, Control_p2[1]);
  // MIPS_ALU mips_alu_1: pin names not known; wires that end beside it: registerfile_1_p5, multiplexer_3_out, ALU_Control_p2, mips_alu_1_p4, mips_alu_1_p5, registerfile_1_p6, Control_p2[7]
  Multiplexer #(.width(32), .enable("false")) multiplexer_4 (
    .in0(adder_1_p3), .in1(adder_2_p3), .out(multiplexer_4_out), .sel(and_1_out));
  Multiplexer #(.width(32), .enable("false")) multiplexer_5 (
    .in0(mips_alu_1_p5), .in1(mips_ram_1_p4), .out(mipsprogramrom_1_p3), .sel(Control_p2[3]));
  // MIPS_RAM mips_ram_1: pin names not known; wires that end beside it: Control_p2[2], clock, in_1, mips_ram_1_p4

  // Other names for the same wires on the sheet: reset = in_1

  // Notes on the sheet:
  //   10 = signExtend
  //   8 = aluSRC
  //   1 = branch
  //   7 =  memWrite
  //   2 = memRead
  //   3 = memToReg
  //   4-6 = ALUop
  //   9 = regWrite/WriteEnable
  //   0 = regDST
  //   address
  //   rs
  //   rt
  //   rd
  //   immediate
  //   shamt
  //   funct
  //   opcode
endmodule
